# Fritzing sketch Circuit (saved by Fritzing 0.9.3b)

parts:
  Arduino = Arduino Uno (Rev3) - ICSP
  RB-FEE-24 = IC, SIP package, 5 pins [chip_label=RB-FEE-24]
  SSD1351_OLED_LCD = IC, SIP package, 11 pins [chip_label=SSD1351]
  Part1 = Bluetooth HC-05 Macho
  Laser_Emitter = SIP - 2 pins [chip_label=HLM1230 package="SIP (Single Inline) [THT]"]

nets:
  N1: Arduino.ICSP_MISO, Arduino.D12/MISO, SSD1351_OLED_LCD.pin5
  5V: Arduino.5V, RB-FEE-24.pin1, SSD1351_OLED_LCD.pin10, Part1.VCC, Laser_Emitter.pin1
  N2: Arduino.ICSP_MOSI, Arduino.D11_PWM/MOSI, SSD1351_OLED_LCD.pin4
  GND: Arduino.GND, RB-FEE-24.pin4, SSD1351_OLED_LCD.pin11, Part1.GND, Laser_Emitter.pin2
  N3: Arduino.D8, SSD1351_OLED_LCD.pin2
  N4: Arduino.D9_PWM, SSD1351_OLED_LCD.pin1
  N5: Arduino.D10_PWM/SS, SSD1351_OLED_LCD.pin3
  N6: Arduino.D0/RX, Part1.RXD
  N7: Arduino.D1/TX, Part1.TXD
  N8: Arduino.D2, RB-FEE-24.pin2
  N9: Arduino.D3_PWM, RB-FEE-24.pin3
  N10: Arduino.D4, RB-FEE-24.pin5
